# Fritzing sketch Calunium (saved by Fritzing 0.6.2b)
stripboards: 1

parts:
  J7 = female pin header, 3 pins [form="♂ (male)"]
  J8 = female pin header, 3 pins [form="♂ (male)"]
  U2 = Mystery_Part___40_pins
  J9 = Generic_female_header___6_pins [form="♀ (female)"]
  J10 = Generic_female_header___8_pins
  J12 = female pin header, 20 pins [form="♀ (female)"]
  J13 = Generic_female_header___8_pins
  XTAL1 = Crystal [frequency="16 Mhz" package=THT]
  J11 = female pin header, 20 pins [form="♀ (female)"]
  C2 = Ceramic Capacitor [capacitance=10pF voltage=50V package="200 mil [THT, multilayer]"]
  C3 = Ceramic_Capacitor
  J14 = Generic_female_header___8_pins
  J16 = Generic_female_header___8_pins [form="♀ (female)"]
  J18 = female pin header, 3 pins [form="♂ (male)"]
  J21 = female pin header, 3 pins [form="♂ (male)"]
  S1 = Pushbutton [package="[THT]"]
  Q1 = NPN_Transistor [part_number=2N7002]
  R1 = Resistor [tolerance=±5% resistance=1k package=THT]
  LED1 = green LED - 5mm [package="5 mm [THT]"]
  LED2 = Red LED - 5mm [package="5 mm [THT]"]
  R2 = Resistor [tolerance=±5% resistance=220 package=THT]
  J23 = female pin header, 2 pins [form="♂ (male)"]
  C4 = Ceramic Capacitor [capacitance=100nF voltage=50V package="100 mil [THT, multilayer]"]
  J25 = female pin header, 2 pins [form="♂ (male)"]
  J24 = Generic_female_header___6_pins [form="♂ (male)"]
  R3 = Resistor [tolerance=±5% resistance=10k package=THT]
  F1 = Temperature_Sensor__Thermistor
  J17 = female pin header, 3 pins [form="♀ (female)"]
  C5 = Ceramic Capacitor [capacitance=100nF package="100 mil [THT, multilayer]"]
  C7 = Electrolytic Capacitor [capacitance=0.1mF package="100 mil [THT, electrolytic]"]
  C8 = Ceramic Capacitor [capacitance=100nF package="100 mil [THT, multilayer]"]
  U3 = Voltage_Regulator___5V [part_number=MCP1702]
  C19 = Ceramic Capacitor [capacitance=100nF package="100 mil [THT, multilayer]"]
  C22 = Ceramic Capacitor [capacitance=100nF package="100 mil [THT, multilayer]"]
  C23 = Ceramic Capacitor [capacitance=100nF package="100 mil [THT, multilayer]"]
  D1 = Rectifier Diode [part_number=1N4001 package="300 mil [THT]"]

nets:
  N1: J7.pin1, U2.connector6, J12.pin7, J16.connector4
  N2: J7.pin2, U2.connector7, J12.pin8, J16.connector5, Q1.connector1
  N3: J7.pin3, U2.connector8, J9.connector0, J12.pin9, S1.Pin_1, S1.Pin_2, C4.1, R3.Pin_1, J17.pin3
  N4: J8.pin1, U2.connector9, U2.connector29, J9.connector2, J12.pin10, J11.pin11, LED1.anode, LED2.anode, R3.Pin_0, F1.connector1, J17.pin1, C7.+, C8.0, U3.connector1, C19.1, C22.1, C23.0, D1.cathode
  N5: J8.pin2, U2.connector5, J12.pin6, J16.connector3
  N6: J8.pin3, U2.connector10, U2.connector30, J9.connector3, J9.connector4, J12.pin11, J11.pin10, C2.1, C3.connector1, S1.Pin_3, S1.Pin_4, Q1.connector0, R2.Pin_1, J24.connector5, J17.pin2, C5.0, C7.-, C8.1, U3.connector0, C22.0, C23.1, D1.anode
  N7: U2.connector0, J12.pin1, J13.connector4
  N8: U2.connector1, J12.pin2, J13.connector5
  N9: U2.connector2, J12.pin3, J13.connector6
  N10: U2.connector3, J12.pin4, J13.connector7
  N11: U2.connector4, J12.pin5, J16.connector2
  N12: U2.connector11, J12.pin12, XTAL1.pin_1, C3.connector0
  N13: U2.connector12, J12.pin13, XTAL1.pin_0, C2.0
  N14: U2.connector13, J12.pin14, J13.connector0, J24.connector2
  N15: U2.connector14, J12.pin15, J13.connector1, J24.connector1
  N16: U2.connector15, J12.pin16, J13.connector2, J14.connector2
  N17: U2.connector16, J12.pin17, J13.connector3, J14.connector3
  N18: U2.connector17, J12.pin18
  N19: U2.connector18, J12.pin19, J16.connector1
  N20: U2.connector19, J12.pin20, J16.connector0
  N21: U2.connector20, J11.pin20, J14.connector5
  N22: U2.connector21, J11.pin19, J14.connector0, J21.pin1
  N23: U2.connector22, J11.pin18, J14.connector1, J18.pin3
  N24: U2.connector23, J11.pin17
  N25: U2.connector24, J11.pin16
  N26: U2.connector25, J11.pin15
  N27: U2.connector26, J11.pin14
  N28: U2.connector27, J11.pin13
  N29: U2.connector28, J11.pin12
  N30: U2.connector31, J11.pin9, J16.connector7, C5.1
  N31: U2.connector32, J10.connector7, J11.pin8
  N32: U2.connector33, J10.connector6, J11.pin7
  N33: U2.connector34, J11.pin6, J21.pin3
  N34: U2.connector35, J11.pin5, J18.pin1
  N35: U2.connector36, J10.connector3, J11.pin4
  N36: U2.connector37, J10.connector2, J11.pin3
  N37: U2.connector38, J10.connector0, J11.pin2
  N38: U2.connector39, J10.connector1, J11.pin1
  N39: J9.connector1, U3.connector2, C19.0
  N40: J10.connector4, J18.pin2
  N41: J10.connector5, J21.pin2
  N42: Q1.connector2, R1.Pin_0
  N43: R1.Pin_1, LED1.cathode
  N44: LED2.cathode, R2.Pin_0
  N45: J23.pin1, J24.connector0
  N46: J23.pin2, C4.0
  N47: J25.pin1, J24.connector3
  N48: J25.pin2, F1.connector0
