# Fritzing sketch Calunium (saved by Fritzing 0.6.2b)
stripboards: 1

parts:
  J7 = female pin header, 3 pins [form="♂ (male)"]
  J8 = female pin header, 3 pins [form="♂ (male)"]
  U2 = Mystery Part - 40 pins [package=THT]
  J9 = Generic female header - 6 pins [form="♀ (female)" package=THT]
  J10 = Generic female header - 8 pins [package=THT]
  J12 = female pin header, 20 pins [form="♀ (female)"]
  J13 = Generic female header - 8 pins [package=THT]
  XTAL1 = Crystal [frequency="16 Mhz" package=THT]
  J11 = female pin header, 20 pins [form="♀ (female)"]
  C2 = Ceramic Capacitor [capacitance=10pF voltage=50V package="200 mil [THT, multilayer]"]
  C3 = Ceramic Capacitor [package="200 mil [THT, multilayer]"]
  J14 = Generic female header - 8 pins [package=THT]
  J16 = Generic female header - 8 pins [form="♀ (female)" package=THT]
  J18 = female pin header, 3 pins [form="♂ (male)"]
  J21 = female pin header, 3 pins [form="♂ (male)"]
  S1 = Pushbutton [package="[THT]"]
  Q1 = NPN-Transistor [part_number=2N7002 package="TO92 [THT]"]
  R1 = Resistor [tolerance=±5% resistance=1k package=THT]
  LED1 = green LED - 5mm [package="5 mm [THT]"]
  LED2 = Red LED - 5mm [package="5 mm [THT]"]
  R2 = Resistor [tolerance=±5% resistance=220 package=THT]
  J23 = female pin header, 2 pins [form="♂ (male)"]
  C4 = Ceramic Capacitor [capacitance=100nF voltage=50V package="100 mil [THT, multilayer]"]
  J25 = female pin header, 2 pins [form="♂ (male)"]
  J24 = Generic female header - 6 pins [form="♂ (male)" package=THT]
  R3 = Resistor [tolerance=±5% resistance=10k package=THT]
  F1 = Temperature Sensor (Thermistor) [package=THT]
  J17 = female pin header, 3 pins [form="♀ (female)"]
  C5 = Ceramic Capacitor [capacitance=100nF package="100 mil [THT, multilayer]"]
  C7 = Electrolytic Capacitor [capacitance=0.1mF package="100 mil [THT, electrolytic]"]
  C8 = Ceramic Capacitor [capacitance=100nF package="100 mil [THT, multilayer]"]
  U3 = Voltage Regulator - 5V [part_number=MCP1702 package="TO92 [THT]"]
  C19 = Ceramic Capacitor [capacitance=100nF package="100 mil [THT, multilayer]"]
  C22 = Ceramic Capacitor [capacitance=100nF package="100 mil [THT, multilayer]"]
  C23 = Ceramic Capacitor [capacitance=100nF package="100 mil [THT, multilayer]"]
  D1 = Rectifier Diode [part_number=1N4001 package="300 mil [THT]"]

nets:
  N1: J7.pin1, U2.pin7, J12.pin7, J16.pin5
  N2: J7.pin2, U2.pin8, J12.pin8, J16.pin6, Q1.G
  N3: J7.pin3, U2.pin9, J9.pin1, J12.pin9, S1.Pin_1, S1.Pin_2, C4.1, R3.Pin_1, J17.pin3
  N4: J8.pin1, U2.pin10, U2.pin30, J9.pin3, J12.pin10, J11.pin11, LED1.anode, LED2.anode, R3.Pin_0, F1.pin_1, J17.pin1, C7.+, C8.0, U3.Vin, C19.1, C22.1, C23.0, D1.cathode
  N5: J8.pin2, U2.pin6, J12.pin6, J16.pin4
  N6: J8.pin3, U2.pin11, U2.pin31, J9.pin4, J9.pin5, J12.pin11, J11.pin10, C2.1, C3.1, S1.Pin_3, S1.Pin_4, Q1.S, R2.Pin_1, J24.pin6, J17.pin2, C5.0, C7.-, C8.1, U3.GND, C22.0, C23.1, D1.anode
  N7: U2.pin1, J12.pin1, J13.pin5
  N8: U2.pin2, J12.pin2, J13.pin6
  N9: U2.pin3, J12.pin3, J13.pin7
  N10: U2.pin4, J12.pin4, J13.pin8
  N11: U2.pin5, J12.pin5, J16.pin3
  N12: U2.pin12, J12.pin12, XTAL1.pin_1, C3.0
  N13: U2.pin13, J12.pin13, XTAL1.pin_0, C2.0
  N14: U2.pin14, J12.pin14, J13.pin1, J24.pin3
  N15: U2.pin15, J12.pin15, J13.pin2, J24.pin2
  N16: U2.pin16, J12.pin16, J13.pin3, J14.pin3
  N17: U2.pin17, J12.pin17, J13.pin4, J14.pin4
  N18: U2.pin18, J12.pin18
  N19: U2.pin19, J12.pin19, J16.pin2
  N20: U2.pin20, J12.pin20, J16.pin1
  N21: U2.pin21, J11.pin20, J14.pin6
  N22: U2.pin22, J11.pin19, J14.pin1, J21.pin1
  N23: U2.pin23, J11.pin18, J14.pin2, J18.pin3
  N24: U2.pin24, J11.pin17
  N25: U2.pin25, J11.pin16
  N26: U2.pin26, J11.pin15
  N27: U2.pin27, J11.pin14
  N28: U2.pin28, J11.pin13
  N29: U2.pin29, J11.pin12
  N30: U2.pin32, J11.pin9, J16.pin8, C5.1
  N31: U2.pin33, J10.pin8, J11.pin8
  N32: U2.pin34, J10.pin7, J11.pin7
  N33: U2.pin35, J11.pin6, J21.pin3
  N34: U2.pin36, J11.pin5, J18.pin1
  N35: U2.pin37, J10.pin4, J11.pin4
  N36: U2.pin38, J10.pin3, J11.pin3
  N37: U2.pin39, J10.pin1, J11.pin2
  N38: U2.pin40, J10.pin2, J11.pin1
  N39: J9.pin2, U3.Vout, C19.0
  N40: J10.pin5, J18.pin2
  N41: J10.pin6, J21.pin2
  N42: Q1.D, R1.Pin_0
  N43: R1.Pin_1, LED1.cathode
  N44: LED2.cathode, R2.Pin_0
  N45: J23.pin1, J24.pin1
  N46: J23.pin2, C4.0
  N47: J25.pin1, J24.pin4
  N48: J25.pin2, F1.pin_0

custom parts:
  Mystery Part - 40 pins: A dummy, proxy, ersatz, stand-in part for whatever you want. With 40 pins on a 100 mil inline pin header footprint.
  Generic female header - 6 pins: Arduino reset/power header
  Generic female header - 8 pins: Arduino A0-A7 header
  Generic female header - 8 pins: Arduino A0-A7 header
  Ceramic Capacitor: 22 pF multilayer Ceramic Capacitor
  Generic female header - 8 pins: Generic female header
  Generic female header - 8 pins: Arduino header D8-D13
  NPN-Transistor: MOSFET transistor
  Generic female header - 6 pins: FTDI header
  Temperature Sensor (Thermistor): Polyfuse
  Voltage Regulator - 5V: 3V3 DC Voltage Regulator
